# Fritzing sketch Circuitry (saved by Fritzing 0.9.9b)

parts:
  Part1 = Arduino Uno (Rev3) - ICSP
  Barometer = Barometric Pressure Sensor - BMP180 Breakout (GY-68)
  Temp_Sensor = LM35 Temperature Sensor [package="TO92 [THT]"]
  Car_Bat_(12V) = Battery Holders [package=battcon_12mm_pth]
  Main_Switch_(Dashboard) = Round Pushbutton
  2_Amp_Car_fuse = FUSE [package=fuse_5mm]
  R1 = Resistor [tolerance=±5% resistance=1k package="2010 [SMD]"]
  Pushbutton_(Dashboard) = Pushbutton [package="[THT]"]
  LCD_Screen_(16x2) = DeuLigne 1.1 - The Snootlab's LCD shield for Arduino
  Accelerometer = SparkFun IMU Breakout - MPU-9250 [part_number=" SEN-13762"]
  R2 = Resistor [tolerance=±5% resistance=33.3 package="2010 [SMD]"]
  R3 = Resistor [tolerance=±5% resistance=10k package="2010 [SMD]"]

nets:
  N1: Part1.A2, R2.Pin_1, R3.Pin_1
  N2: Part1.ICSP_MISO, Part1.D12/MISO, Barometer.SDA, LCD_Screen_(16x2).A4(SDA), Accelerometer.SDA/SDI
  5V: Part1.5V, Temp_Sensor.+Vs, Pushbutton_(Dashboard).Pin_3, Pushbutton_(Dashboard).Pin_4, LCD_Screen_(16x2).+5V, Accelerometer.VDD
  N3: Part1.GND, R1.Pin_0
  N4: Part1.D8, Temp_Sensor.Vout
  N5: Part1.A5/SCL, Barometer.SCL, LCD_Screen_(16x2).A5(CLK), Accelerometer.SCL/SCLK
  N6: Part1.D2, R1.Pin_1, Pushbutton_(Dashboard).Pin_1, Pushbutton_(Dashboard).Pin_2
  3V3: Part1.3V3, Barometer.VCC
  N7: Part1.VIN, Main_Switch_(Dashboard).leg1, R2.Pin_0
  GND: Barometer.GND, Temp_Sensor.GND, Car_Bat_(12V).-, LCD_Screen_(16x2).GND, Accelerometer.GND, R3.Pin_0
  N8: Car_Bat_(12V).+, 2_Amp_Car_fuse.1
  N9: Main_Switch_(Dashboard).leg0, 2_Amp_Car_fuse.2
